// Logisim project Phase 2.circ as structural Verilog: 1 circuit, main circuit main
module main (
);

  wire A_q, A_qn, and_1_out, and_2_out, and_3_out, and_4_out, and_5_out, and_6_out, and_7_out, B_q, B_qn,
       C_q, C_qn, clock_1_out, D_q, D_qn, n7_segment_display_driver_1_p5, n7_segment_display_driver_1_p6,
       n7_segment_display_driver_1_p7, n7_segment_display_driver_1_p8, n7_segment_display_driver_1_p9,
       n7_segment_display_driver_1_p10, n7_segment_display_driver_1_p11, or_1_out, or_2_out, or_3_out;

  Clock clock_1 (.out(clock_1_out));
  and and_1 (and_1_out, D_q, C_qn, B_qn);
  and and_2 (and_2_out, B_q, D_qn);
  and and_3 (and_3_out, D_qn, C_qn, A_qn);
  and and_4 (and_4_out, D_q, C_q);
  and and_5 (and_5_out, D_qn, B_qn, A_qn);
  and and_6 (and_6_out, D_qn, C_q);
  and and_7 (and_7_out, B_q, D_q);
  or or_1 (or_1_out, and_1_out, and_2_out);
  or or_2 (or_2_out, and_3_out, and_4_out);
  or or_3 (or_3_out, and_5_out, and_6_out);
  D_Flip_Flop A (.clk(clock_1_out), .D(and_7_out), .Q(A_q), .Qn(A_qn), .preset(1'b0), .en(1'b1), .reset(1'b0));
  D_Flip_Flop B (.clk(clock_1_out), .D(or_1_out), .Q(B_q), .Qn(B_qn), .preset(1'b0), .en(1'b1), .reset(1'b0));
  D_Flip_Flop C (.clk(clock_1_out), .D(or_2_out), .Q(C_q), .Qn(C_qn), .preset(1'b0), .en(1'b1), .reset(1'b0));
  D_Flip_Flop D (.clk(clock_1_out), .D(or_3_out), .Q(D_q), .Qn(D_qn), .preset(1'b0), .en(1'b1), .reset(1'b0));
  // _7_segment_display_driver 7_segment_display_driver_1: pin names not known; wires that end beside it: A_q, B_q, C_q, D_q, n7_segment_display_driver_1_p5, n7_segment_display_driver_1_p6, n7_segment_display_driver_1_p7, n7_segment_display_driver_1_p8, n7_segment_display_driver_1_p9, n7_segment_display_driver_1_p10, n7_segment_display_driver_1_p11
  _7_Segment_Display u_7_segment_display_1 (
    .g(n7_segment_display_driver_1_p11), .f(n7_segment_display_driver_1_p10),
    .a(n7_segment_display_driver_1_p5), .b(n7_segment_display_driver_1_p6),
    .e(n7_segment_display_driver_1_p9), .d(n7_segment_display_driver_1_p8), .c(n7_segment_display_driver_1_p7));  // open: dp

  // Notes on the sheet:
  //   D'
  //   D
  //   C'
  //   C
  //   B'
  //   B
  //   A'
  //   A
  //   B
  //   C
  //   D
  //   Our Sequence
  //   0->3->2->1->4->6->5->8
endmodule
